# Fritzing sketch dataLogger (saved by Fritzing 0.9.6b)
circuit board: 8.49489cm x 6.223cm
breadboards: 1

parts:
  PCB2 = RTC_DS1302_module
  U1 = Mystery Part - 4 pins [chip_label="Pololu 3v3 stepdown" package=THT]
  12V = female pin header, 2 pins [form="♀ (female)"]
  R1 = Resistor [tolerance=±5% power=0.25 resistance=100k package=THT]
  R2 = Resistor [tolerance=±5% power=0.25 resistance=1M package=THT]
  MCU1 = ESP32-Pico-D4 [part_number=ESP32-Pico-D4 package=THT]
  S1 = Pushbutton [package="[THT]"]

nets:
  3V3: PCB2.VCC, U1.Vout, MCU1.3v3, MCU1.3V3
  GND: PCB2.GND, U1.GND, 12V.pin1, R1.Pin_0, MCU1.GND, S1.Pin_3, S1.Pin_4
  N1: PCB2.RST, MCU1.IO23
  N2: PCB2.DAT, MCU1.IO22
  N3: PCB2.CLK, MCU1.io21
  N4: U1.Vin, 12V.pin2, R2.Pin_0
  N5: R1.Pin_1, R2.Pin_1, MCU1.IO34
  N6: MCU1.EN, MCU1.5V, S1.Pin_1, S1.Pin_2

custom parts:
  RTC_DS1302_module: Arduino module DS1302 SPI Real Time Clock
  Mystery Part - 4 pins: A dummy, proxy, ersatz, stand-in part for whatever you want. With 4 pins on a 100 mil inline pin header footprint.
  ESP32-Pico-D4: Pins on a pico32 board.
